# Fritzing sketch AS-IF-1 - protoboard - wiring (saved by Fritzing 0.8.7b)
perfboards: 4

parts:
  Composant1 = Arduino Uno (Rev3) - ICSP  # not connected
  JP3 = Header 6 [package=1x06_smd_straight_alt]  # not connected
  JP5 = Header 1 [package=1x01_offset]  # not connected
  JP6 = Header 1 [package=1x01_offset]  # not connected
  JP7 = Header 1 [package=1x01_offset]  # not connected
  JP8 = Header 1 [package=1x01_offset]  # not connected
  JP9 = Header 1 [package=1x01_offset]  # not connected
  JP4 = Header 8 [package=1x08_smd]  # not connected
  JP10 = Header 1 [package=1x01_offset]  # not connected
  JP11 = Header 1 [package=1x01_offset]  # not connected
  JP12 = Header 6 [package=1x06_smd_straight_alt]  # not connected
  JP13 = Header 8 [package=1x08_smd]
  JP14 = Header 1 [package=1x01_offset]  # not connected
  JP15 = Header 1 [package=1x01_offset]  # not connected
  JP16 = Header 1 [package=1x01_offset]  # not connected
  JP17 = Header 1 [package=1x01_offset]  # not connected
  JP18 = Header 1 [package=1x01_offset]  # not connected
  JP19 = Header 1 [package=1x01_offset]  # not connected
  JP20 = Header 1 [package=1x01_offset]  # not connected
  JP21 = Header 1 [package=1x01_offset]  # not connected
  JP22 = Header 1 [package=1x01_offset]  # not connected
  JP23 = Header 1 [package=1x01_offset]  # not connected
  JP24 = Header 1 [package=1x01_offset]  # not connected
  JP25 = Header 1 [package=1x01_offset]  # not connected
  JP26 = Header 1 [package=1x01_offset]  # not connected
  JP27 = Header 1 [package=1x01_offset]  # not connected
  JP28 = Header 1 [package=1x01_offset]  # not connected
  JP29 = Header 1 [package=1x01_offset]  # not connected
  JP30 = Header 1 [package=1x01_offset]  # not connected
  JP31 = Header 1 [package=1x01_offset]  # not connected
  JP32 = Header 1 [package=1x01_offset]  # not connected
  JP33 = Header 1 [package=1x01_offset]  # not connected
  JP34 = Header 1 [package=1x01_offset]  # not connected
  JP35 = Header 1 [package=1x01_offset]  # not connected
  JP36 = Header 1 [package=1x01_offset]  # not connected
  JP37 = Header 1 [package=1x01_offset]
  JP38 = Header 1 [package=1x01_offset]
  JP39 = Header 1 [package=1x01_offset]
  JP40 = Header 1 [package=1x01_offset]
  JP41 = Header 1 [package=1x01_offset]  # not connected
  JP42 = Header 1 [package=1x01_offset]  # not connected
  JP43 = Header 1 [package=1x01_offset]  # not connected
  JP44 = Header 1 [package=1x01_offset]  # not connected
  JP45 = Header 1 [package=1x01_offset]  # not connected
  JP46 = Header 1 [package=1x01_offset]  # not connected
  JP47 = Header 1 [package=1x01_offset]
  JP48 = Header 1 [package=1x01_offset]
  JP49 = Header 1 [package=1x01_offset]  # not connected
  JP50 = Header 1 [package=1x01_offset]  # not connected
  JP53 = Header 8 [package=1x08_smd]
  microSD1 = MicroSD Breakout
  Composant2 = IMU Digital Combo Board 6DOF
  JP54 = Header 8 [package=1x08_smd]
  JP55 = Header 8 [package=1x08_smd]
  JP57 = Header 1 [package=1x01_offset]  # not connected
  JP58 = Header 1 [package=1x01_offset]  # not connected
  JP59 = Header 1 [package=1x01_offset]  # not connected
  JP60 = Header 1 [package=1x01_offset]  # not connected
  JP61 = Header 1 [package=1x01_offset]  # not connected
  JP62 = Header 1 [package=1x01_offset]  # not connected
  JP63 = Header 1 [package=1x01_offset]  # not connected
  JP67 = Header 1 [package=1x01_offset]  # not connected
  JP68 = Header 1 [package=1x01_offset]
  JP69 = Header 1 [package=1x01_offset]  # not connected
  JP70 = Header 1 [package=1x01_offset]
  JP71 = Header 1 [package=1x01_offset]  # not connected
  JP72 = Header 1 [package=1x01_offset]  # not connected
  JP73 = Header 1 [package=1x01_offset]
  JP74 = Header 1 [package=1x01_offset]  # not connected
  JP75 = Header 1 [package=1x01_offset]  # not connected
  JP76 = Header 1 [package=1x01_offset]  # not connected
  JP77 = Header 1 [package=1x01_offset]
  JP78 = Header 1 [package=1x01_offset]  # not connected
  JP81 = Header 1 [package=1x01_offset]  # not connected
  JP83 = Header 1 [package=1x01_offset]  # not connected
  JP85 = Header 1 [package=1x01_offset]
  JP86 = Header 1 [package=1x01_offset]  # not connected
  JP87 = Header 1 [package=1x01_offset]  # not connected
  JP88 = Header 1 [package=1x01_offset]  # not connected
  JP89 = Header 1 [package=1x01_offset]  # not connected
  JP90 = Header 1 [package=1x01_offset]
  JP91 = Header 1 [package=1x01_offset]  # not connected
  JP92 = Header 1 [package=1x01_offset]  # not connected
  JP93 = Header 6 [package=1x06_smd_straight_alt]
  JP94 = Header 6 [package=1x06_smd_straight_alt]  # not connected
  JP95 = Header 1 [package=1x01_offset]  # not connected
  JP96 = Header 1 [package=1x01_offset]  # not connected
  JP97 = Header 8 [package=1x08_smd]  # not connected
  JP98 = Header 1 [package=1x01_offset]  # not connected
  JP99 = Header 1 [package=1x01_offset]  # not connected
  JP100 = Header 1 [package=1x01_offset]  # not connected
  JP101 = Header 1 [package=1x01_offset]  # not connected
  JP102 = Header 1 [package=1x01_offset]  # not connected
  microSD2 = MicroSD Breakout  # not connected
  JP103 = Header 1 [package=1x01_offset]
  JP104 = Header 1 [package=1x01_offset]
  JP105 = Header 1 [package=1x01_offset]
  JP106 = Header 1 [package=1x01_offset]
  JP107 = Header 1 [package=1x01_offset]
  JP65 = Header 1 [package=1x01_offset]  # not connected
  JP84 = Header 1 [package=1x01_offset]  # not connected
  JP79 = Header 1 [package=1x01_offset]  # not connected
  Composant3 = FTDI Basic Programmer

nets:
  N1: JP13.7, Composant3.TXO
  N2: JP13.8, Composant3.RXI
  N3: JP37.1, Composant2.3.3V
  N4: JP38.1, Composant2.GND
  N5: JP39.1, Composant2.SCL
  N6: JP40.1, Composant2.SDA
  N7: JP47.1, Composant2.INT1
  N8: JP48.1, Composant2.INT0
  N9: JP53.1, microSD1.5V
  N10: JP53.3, microSD1.GND
  N11: JP53.4, microSD1.CLK
  N12: JP53.5, microSD1.DO
  N13: JP53.6, microSD1.DI
  N14: JP53.7, microSD1.CS
  N15: JP54.1, JP103.1
  N16: JP54.3, JP105.1
  N17: JP54.4, JP107.1
  N18: JP54.5, JP104.1
  N19: JP54.6, JP106.1
  N20: JP54.7, JP55.5
  N21: JP68.1, JP77.1
  N22: JP70.1, JP85.1
  N23: JP73.1, JP93.5
  N24: JP90.1, JP93.4

notes:
  NOTE : Pins shown here are limited to the pins necessary for AS-IF, and match in position the pins of Arduino UNO
  8 pin connector to SD board
  CLK to SCK (grey)
  DO to MISO (pink)
  DI to MOSI (cyan)
  CS to PIN4 (white)
  GND to GND (black)
  VCC to 5V (red)
  PAYLOAD plate, from below
  PAYLOAD plate, from above
  MASTER plate, from below
  MASTER plate, from above

custom parts:
  MicroSD Breakout: 5V-ready microSD Breakout with Level Shifter
